// Logisim project DL PRO 4..circ as structural Verilog: 1 circuit, main circuit main
module main (
  input  J,
  input  K,
  input  D,
  input  T,
  output out_5,
  output out_6,
  output out_7,
  output out_8,
  output out_9,
  output out_10
);

  wire clock_1_out, clock_2_out, clock_3_out;

  Clock clock_1 (.out(clock_1_out));
  Clock clock_2 (.out(clock_2_out));
  Clock clock_3 (.out(clock_3_out));
  J_K_Flip_Flop j_k_ff_1 (.J(J), .clk(clock_1_out), .K(K), .Q(out_5), .Qn(out_6));  // open: preset, en, reset
  D_Flip_Flop d_ff_1 (.clk(clock_2_out), .D(D), .Q(out_7), .Qn(out_8));  // open: preset, en, reset
  T_Flip_Flop t_ff_1 (.clk(clock_3_out), .T(T), .Q(out_9), .Qn(out_10));  // open: preset, reset, en

  // Notes on the sheet:
  //   15.
  //   CLOCK
  //   CLOCK
  //   CLOCK
  //   JK FLIP FLOP
  //   D FLIP FLOP
  //   T FLIP FLOP
endmodule
