// Logisim project DL PROGRAM 1.circ as structural Verilog: 1 circuit, main circuit main
module main (
  input  _1_AND_GATE,
  input  _2__OR_GATE,
  input  _3__NOT_GATE,
  input  _4__NAND_GATE,
  input  in_5,
  input  in_6,
  input  _5__XOR_GATE,
  input  _4__NOR_GATE,
  input  in_9,
  input  _5__XNOR_GATE,
  input  in_11,
  input  in_12,
  input  in_13,
  output out_14,
  output out_15,
  output out_16,
  output out_17,
  output out_18,
  output out_19,
  output out_20
);

  and and_1 (out_14, _1_AND_GATE, _3__NOT_GATE);
  not not_1 (out_16, in_6);
  nor nor_1 (out_18, _4__NOR_GATE, _5__XNOR_GATE);
  xnor xnor_1 (out_20, in_12, in_13);
  or or_1 (out_15, _2__OR_GATE, _4__NAND_GATE);
  nand nand_1 (out_17, in_5, _5__XOR_GATE);
  xor xor_1 (out_19, in_9, in_11);

  // Notes on the sheet:
  //   PROGRAM:1
endmodule
